// Logisim project part1.circ as structural Verilog
module Ex1 (
  input  [7:0] Input_1,
  output [7:0] Out2
);

  wire [7:0] xor_1_out;

  assign xor_1_out = Input_1 ^ {8{1'b1}};  // XOR_Gate xor_1, 8 bits wide
  Adder adder_1 (.a(xor_1_out), .b(8'h1), .out(Out2));  // open: cin, cout
endmodule

module RR (
  input  [15:0] in_1,
  input  [3:0] in_2,
  output [15:0] out_3,
  output [3:0] out_4
);

  wire [3:0] subtractor_1_out;
  wire [15:0] shifter_1_out, shifter_2_out;

  Subtractor #(.width(4)) subtractor_1 (.a(4'b1111), .b(in_2), .out(subtractor_1_out));  // open: bin, bout
  Adder #(.width(4)) adder_1 (.a(subtractor_1_out), .b(4'b0001), .out(out_4));  // open: cin, cout
  Shifter #(.width(16), .shift("lr")) shifter_1 (.in(in_1), .\dist (in_2), .out(shifter_1_out));
  Shifter #(.width(16)) shifter_2 (.in(in_1), .\dist (out_4), .out(shifter_2_out));
  assign out_3 = shifter_1_out | shifter_2_out;  // OR_Gate or_1, 16 bits wide
endmodule
