// Logisim project fib.circ as structural Verilog: 1 circuit, main circuit main
module main (
  input  in_1,
  input  in_2
);

  wire button_1_out, clock_1_out, comparator_1_lt, comparator_2_eq;
  wire [15:0] adder_1_out, counter_1_q, or_1_out, register_1_q, register_2_q, register_3_q;

  Clock clock_1 (.out(clock_1_out));
  Counter #(.width(16), .max('hf), .ongoal("stay")) counter_1 (
    .load(in_1), .Q(counter_1_q), .clk(clock_1_out), .clr(button_1_out));  // open: D, count, carry
  Button button_1 (.out(button_1_out));
  Comparator #(.width(16)) comparator_1 (.a(counter_1_q), .b(16'he), .lt(comparator_1_lt));  // open: gt, eq
  Comparator #(.width(16)) comparator_2 (.a(counter_1_q), .b(16'hf), .eq(comparator_2_eq));  // open: gt, lt
  Adder #(.width(16)) adder_1 (.a(register_3_q), .b(register_1_q), .out(adder_1_out), .cin(in_2));  // open: cout
  Register #(.width(16)) register_1 (
    .D(adder_1_out), .Q(register_1_q), .clk(clock_1_out), .clr(comparator_2_eq));  // open: en
  assign or_1_out = adder_1_out | register_2_q;  // OR_Gate or_1, 16 bits wide
  // Probe on or_1_out
  Register #(.width(16)) register_2 (
    .D(or_1_out), .Q(register_2_q), .clk(clock_1_out), .clr(comparator_1_lt));  // open: en
  Register #(.width(16)) register_3 (
    .D(register_1_q), .Q(register_3_q), .clk(clock_1_out), .clr(comparator_2_eq));  // open: en
endmodule
