// Logisim project cpu.circ as structural Verilog: 1 circuit, main circuit main
module main (
  input  [31:0] RS_READ_VALUE,
  input  [31:0] RT_READ_VALUE,
  input  [31:0] INSTRUCTION,
  input  CLOCK,
  input  RESET,
  input  op,
  input  op_2,
  input  op_3,
  output [31:0] t0,
  output [31:0] t1,
  output [31:0] t2,
  output [31:0] t3,
  output [4:0] RS,
  output [4:0] RT,
  output [4:0] Write_Register,
  output [31:0] RD_WRITE_VALUE,
  output RD_WRITE_ENABLE,
  output [23:0] FETCH_ADDRESS,
  output MemWrite
);

  wire _2addu, _2and, _2or, _3addu, _4add, add, addiu, addu, ALU_equal, ALU_signed_overflow, \and , andi,
       beq, beq_true, bitpal, bne, bne_true, branch_true, \byte , comparator_1_eq, comparator_2_eq,
       comparator_3_eq, comparator_4_eq, comparator_5_eq, comparator_6_eq, comparator_7_eq, comparator_8_eq,
       comparator_22_eq, comparator_23_eq, comparator_24_eq, comparator_25_eq, comparator_26_eq,
       comparator_27_eq, comparator_28_eq, comparator_29_eq, comparator_30_eq, comparator_31_eq,
       comparator_32_eq, comparator_33_eq, comparator_34_eq, comparator_35_eq, comparator_36_eq,
       comparator_37_eq, comparator_38_eq, comparator_39_eq, is_nop, itype, j, jal, jr, Jtype, jump, lb, lbu,
       lfsr, lui, lw, MemtoReg, Memwrite_t, not_4_out, not_5_out, \or , or_3_out, or_4_out, or_7_out,
       or_15_out, or_16_out, ori, rs_not_t, rt_not_t, Rtype, shift, sll, slt, sltu, sra, srl, sub, subu,
       t_write_enable, undriven, write_dst_not_t, zero_ext;
  wire [1:0] bit_extender_3_out, bit_extender_4_out, branch_value, choose, jr_value, jump_value, regwrite;
  wire [3:0] multiplexer_1_out, multiplexer_2_out, multiplexer_3_out, multiplexer_4_out, multiplexer_5_out,
       multiplexer_6_out, multiplexer_7_out, multiplexer_10_out, multiplexer_11_out, multiplexer_12_out,
       multiplexer_13_out, multiplexer_14_out, multiplexer_15_out, switch2;
  wire [4:0] rd, shamt, subtractor_3_out, subtractor_4_out, subtractor_5_out, write_dst;
  wire [5:0] funct, op_t, switch;
  wire [15:0] immediate;
  wire [23:0] adder_1_out, adder_2_out, adder_3_out, adder_4_out, bit_extender_2_out, next_pccount,
       subtractor_1_out, subtractor_2_out;
  wire [25:0] addresss;
  wire [31:0] alu_result, ALU_result_2, and_2_out, and_3_out, and_4_out, and_5_out, and_6_out, and_7_out,
       and_8_out, and_9_out, bit_extender_1_out, bit_extender_5_out, bit_extender_6_out, bit_extender_7_out,
       bit_extender_17_out, Data1, Data2, Data_imme, dataout, INSTRUCTION_t, lui_imme, Mem_out,
       multiplexer_16_out, multiplexer_22_out, multiplexer_23_out, multiplexer_26_out, rsout0, rtout0,
       shifter_2_out, shifter_3_out, shifter_4_out, shifter_5_out, shifter_6_out, shifter_7_out,
       shifter_8_out, shifter_9_out, shifter_10_out, shifter_11_out, shifter_12_out;

  Multiplexer #(.width(4)) multiplexer_1 (
    .in0(4'b0000), .in1(4'b0001), .out(multiplexer_1_out), .sel(sll));  // open: en
  Multiplexer #(.width(4)) multiplexer_2 (
    .in0(4'b0000), .in1(4'b0010), .out(multiplexer_2_out), .sel(srl));  // open: en
  Multiplexer #(.width(4)) multiplexer_3 (
    .in0(4'b0000), .in1(4'b0011), .out(multiplexer_3_out), .sel(sra));  // open: en
  Multiplexer #(.width(4)) multiplexer_4 (
    .in0(4'b0000), .in1(4'b0100), .out(multiplexer_4_out), .sel(_4add));  // open: en
  Multiplexer #(.width(4)) multiplexer_5 (
    .in0(4'b0000), .in1(4'b0101), .out(multiplexer_5_out), .sel(_3addu));  // open: en
  Multiplexer #(.width(4)) multiplexer_6 (
    .in0(4'b0000), .in1(4'b0110), .out(multiplexer_6_out), .sel(sub));  // open: en
  Multiplexer #(.width(4)) multiplexer_7 (
    .in0(4'b0000), .in1(4'b1101), .out(multiplexer_7_out), .sel(lfsr));  // open: en
  Comparator #(.width(5), .mode("unsigned")) comparator_1 (.a(RS), .b(5'b01000), .eq(comparator_1_eq));  // open: gt, lt
  Comparator #(.width(5), .mode("unsigned")) comparator_2 (.a(RS), .b(5'b01001), .eq(comparator_2_eq));  // open: gt, lt
  Comparator #(.width(5), .mode("unsigned")) comparator_3 (.a(RS), .b(5'b01010), .eq(comparator_3_eq));  // open: gt, lt
  Comparator #(.width(5), .mode("unsigned")) comparator_4 (.a(RS), .b(5'b01011), .eq(comparator_4_eq));  // open: gt, lt
  Comparator #(.width(5), .mode("unsigned")) comparator_5 (.a(RT), .b(5'b01000), .eq(comparator_5_eq));  // open: gt, lt
  Comparator #(.width(5), .mode("unsigned")) comparator_6 (.a(RT), .b(5'b01001), .eq(comparator_6_eq));  // open: gt, lt
  Comparator #(.width(5), .mode("unsigned")) comparator_7 (.a(RT), .b(5'b01010), .eq(comparator_7_eq));  // open: gt, lt
  Comparator #(.width(5), .mode("unsigned")) comparator_8 (.a(RT), .b(5'b01011), .eq(comparator_8_eq));  // open: gt, lt
  assign switch2 = multiplexer_1_out & multiplexer_2_out & multiplexer_3_out & multiplexer_4_out & multiplexer_5_out & multiplexer_6_out & multiplexer_7_out & multiplexer_10_out & multiplexer_11_out & multiplexer_12_out & multiplexer_13_out & multiplexer_14_out & multiplexer_15_out;  // AND_Gate and_1, 4 bits wide
  assign bit_extender_1_out = {{16{1'b0}}, immediate};  // Bit_Extender bit_extender_1
  or or_1 (\byte , lb, lbu);
  or or_2 (MemtoReg, lbu, lb, lw);
  Multiplexer #(.width(32)) multiplexer_8 (
    .in0(alu_result), .in1(Mem_out), .out(RD_WRITE_VALUE), .sel(MemtoReg));  // open: en
  Multiplexer #(.width(5)) multiplexer_9 (.in0(RT), .in1(rd), .out(write_dst), .sel(Rtype));  // open: en
  Register #(.width(24)) register_1 (.D(next_pccount), .Q(FETCH_ADDRESS), .clk(CLOCK));  // open: en, clr
  // Probe on FETCH_ADDRESS
  or or_3 (or_3_out, comparator_1_eq, comparator_2_eq, comparator_3_eq, comparator_4_eq);
  or or_4 (or_4_out, comparator_5_eq, comparator_6_eq, comparator_7_eq, comparator_8_eq);
  or or_5 (zero_ext, addiu, lbu);
  Shifter #(.width(32)) shifter_1 (.in(bit_extender_1_out), .\dist (5'b10000), .out(lui_imme));
  // Probe on lui_imme
  mem_main MEM (
    .Data_Mem_Addr(alu_result), .Data_Mem_In(Data2), .ACCESS_BYTE(\byte ), .CLOCK(Memwrite_t),
    .MEM_WRITE(CLOCK), .Data_Mem_Out(dataout));
  Adder #(.width(24)) adder_1 (.a(FETCH_ADDRESS), .b(24'h1), .out(adder_1_out));  // open: cin, cout
  Adder #(.width(24)) adder_2 (.a(FETCH_ADDRESS), .b(24'h1), .out(adder_2_out));  // open: cin, cout
  Adder #(.width(24)) adder_3 (.a(adder_2_out), .b(bit_extender_2_out), .out(adder_3_out));  // open: cin, cout
  assign bit_extender_2_out = {{8{immediate[15]}}, immediate};  // Bit_Extender bit_extender_2
  Subtractor #(.width(24)) subtractor_1 (
    .a(addresss[23:0]), .b(24'h100000), .out(subtractor_1_out));  // open: bin, bout
  Subtractor #(.width(24)) subtractor_2 (.a(Data1[23:0]), .b(24'h100000), .out(subtractor_2_out));  // open: bin, bout
  Comparator #(.width(6)) comparator_9 (.a(op_t), .b({6{1'b0}}), .eq(Rtype));  // open: gt, lt
  Comparator #(.width(6)) comparator_10 (.a(op_t), .b(6'b000010), .eq(j));  // open: gt, lt
  Comparator #(.width(6)) comparator_11 (.a(op_t), .b(6'b000011), .eq(jal));  // open: gt, lt
  Comparator #(.width(6)) comparator_12 (.a(op_t), .b(6'b001001), .eq(addiu));  // open: gt, lt
  Comparator #(.width(6)) comparator_13 (.a(op_t), .b(6'b001100), .eq(andi));  // open: gt, lt
  Comparator #(.width(6)) comparator_14 (.a(op_t), .b(6'b001101), .eq(ori));  // open: gt, lt
  Comparator #(.width(6)) comparator_15 (.a(op_t), .b(6'b001111), .eq(lui));  // open: gt, lt
  Comparator #(.width(6)) comparator_16 (.a(op_t), .b(6'b100000), .eq(lb));  // open: gt, lt
  Comparator #(.width(6)) comparator_17 (.a(op_t), .b(6'b100100), .eq(lbu));  // open: gt, lt
  Comparator #(.width(6)) comparator_18 (.a(op_t), .b(6'b100011), .eq(lw));  // open: gt, lt
  Comparator #(.width(6)) comparator_19 (.a(op_t), .b(6'b101011), .eq(Memwrite_t));  // open: gt, lt
  Comparator #(.width(6)) comparator_20 (.a(op_t), .b(6'b000100), .eq(beq));  // open: gt, lt
  Comparator #(.width(6)) comparator_21 (.a(op_t), .b(6'b000101), .eq(bne));  // open: gt, lt
  not not_1 (rs_not_t, or_3_out);
  not not_2 (rt_not_t, or_4_out);
  Multiplexer #(.width(4)) multiplexer_10 (
    .in0(4'b0000), .in1(4'b0111), .out(multiplexer_10_out), .sel(subu));  // open: en
  Multiplexer #(.width(4)) multiplexer_11 (
    .in0(4'b0000), .in1(4'b1000), .out(multiplexer_11_out), .sel(_2and));  // open: en
  Multiplexer #(.width(4)) multiplexer_12 (
    .in0(4'b0000), .in1(4'b1001), .out(multiplexer_12_out), .sel(_2or));  // open: en
  Multiplexer #(.width(4)) multiplexer_13 (
    .in0(4'b0000), .in1(4'b1010), .out(multiplexer_13_out), .sel(slt));  // open: en
  Multiplexer #(.width(4)) multiplexer_14 (
    .in0(4'b0000), .in1(4'b1011), .out(multiplexer_14_out), .sel(sltu));  // open: en
  Multiplexer #(.width(4)) multiplexer_15 (
    .in0(4'b0000), .in1(4'b1100), .out(multiplexer_15_out), .sel(bitpal));  // open: en
  Multiplexer #(.width(32)) multiplexer_16 (
    .in0(INSTRUCTION), .in1({32{1'b0}}), .out(multiplexer_16_out), .sel(is_nop));  // open: en
  or or_6 (Jtype, j, jal);
  Subtractor #(.width(5)) subtractor_3 (.a(RS), .b(5'b01000), .out(subtractor_3_out));  // open: bin, bout
  Subtractor #(.width(5)) subtractor_4 (.a(RT), .b(5'b01000), .out(subtractor_4_out));  // open: bin, bout
  Multiplexer #(.select(2), .width(24)) multiplexer_17 (
    .in0(adder_1_out), .in2(adder_3_out), .in3(subtractor_1_out), .out(next_pccount), .sel(choose));  // open: in1, en
  Register #(.width(32)) register_2 (.D(multiplexer_16_out), .Q(INSTRUCTION_t), .clk(CLOCK));  // open: en, clr
  Bit_Extender #(.in_width(5), .out_width(2)) bit_extender_3 (.in(subtractor_3_out), .out(bit_extender_3_out));
  Bit_Extender #(.in_width(5), .out_width(2)) bit_extender_4 (.in(subtractor_4_out), .out(bit_extender_4_out));
  Adder #(.width(24)) adder_4 (.a(FETCH_ADDRESS), .b(24'h1), .out(adder_4_out));  // open: cin, cout
  assign bit_extender_5_out = {{8{adder_4_out[23]}}, adder_4_out};  // Bit_Extender bit_extender_5
  or or_7 (or_7_out, Jtype, Rtype);
  assign bit_extender_6_out = {{16{1'b0}}, immediate};  // Bit_Extender bit_extender_6
  assign bit_extender_7_out = {{16{immediate[15]}}, immediate};  // Bit_Extender bit_extender_7
  Multiplexer #(.select(4), .width(6)) multiplexer_18 (
    .in1({6{1'b0}}), .in2(6'b000010), .in3(6'b000011), .in4(6'b100000), .in5(6'b100001), .in6(6'b100010),
    .in7(6'b100011), .in8(6'b100100), .in9(6'b100101), .in10(6'b101010), .in11(6'b101011), .in12(6'b111110),
    .in13({6{1'b1}}), .out(switch), .sel(switch2));  // open: in0, in14, in15, en
  Multiplexer #(.width(5)) multiplexer_19 (
    .in0(write_dst), .in1({5{1'b1}}), .out(Write_Register), .sel(jal));  // open: en
  Subtractor #(.width(5)) subtractor_5 (.a(write_dst), .b(5'b01000), .out(subtractor_5_out));  // open: bin, bout
  not not_3 (itype, or_7_out);
  regfile_main RegFile (
    .Read_register_1(bit_extender_3_out), .Read_register_2(bit_extender_4_out), .write_register(regwrite),
    .write_data(RD_WRITE_VALUE), .t0_Value(t0), .t1_Value(t1), .t2_Value(t2), .t3_Value(t3),
    .RegWrite(t_write_enable), .clock(CLOCK), .Read_Data_1(rsout0), .Read_Data_2(rtout0));
  Multiplexer #(.width(32)) multiplexer_20 (
    .in0(bit_extender_6_out), .in1(bit_extender_7_out), .out(Data_imme), .sel(zero_ext));  // open: en
  Bit_Extender #(.in_width(5), .out_width(2)) bit_extender_8 (.in(subtractor_5_out), .out(regwrite));
  Multiplexer #(.width(32)) multiplexer_21 (
    .in0(RD_WRITE_VALUE), .in1(bit_extender_5_out), .out(RD_WRITE_VALUE), .sel(jal));  // open: en
  Shifter #(.width(32)) shifter_2 (.in(dataout), .\dist (5'b11000), .out(shifter_2_out));
  or or_8 (is_nop, branch_true, jump, jr);
  or or_9 (shift, sll, srl, sra);
  Multiplexer #(.width(32)) multiplexer_22 (
    .in0(Data_imme), .in1(Data2), .out(multiplexer_22_out), .sel(Rtype));  // open: en
  Shifter #(.width(32), .shift("lr")) shifter_3 (.in(shifter_2_out), .\dist (5'b11000), .out(shifter_3_out));
  Shifter #(.width(32), .shift("ar")) shifter_4 (.in(shifter_2_out), .\dist (5'b11000), .out(shifter_4_out));
  assign and_2_out = INSTRUCTION_t & 32'hfc000000;  // AND_Gate and_2, 32 bits wide
  assign and_3_out = INSTRUCTION_t & 32'h3e00000;  // AND_Gate and_3, 32 bits wide
  assign and_4_out = INSTRUCTION_t & 32'h1f0000;  // AND_Gate and_4, 32 bits wide
  assign and_5_out = INSTRUCTION_t & 32'hf800;  // AND_Gate and_5, 32 bits wide
  assign and_6_out = INSTRUCTION_t & 32'h7c00;  // AND_Gate and_6, 32 bits wide
  assign and_7_out = INSTRUCTION_t & 32'h3f;  // AND_Gate and_7, 32 bits wide
  assign and_8_out = INSTRUCTION_t & 32'hffff;  // AND_Gate and_8, 32 bits wide
  assign and_9_out = INSTRUCTION_t & 32'h3ffffff;  // AND_Gate and_9, 32 bits wide
  and u_bne_true (bne_true, bne, not_4_out);
  Multiplexer #(.width(32)) multiplexer_23 (
    .in0(shifter_3_out), .in1(shifter_4_out), .out(multiplexer_23_out), .sel(lb));  // open: en
  Shifter #(.width(32), .shift("lr")) shifter_5 (.in(and_2_out), .\dist (5'b11010), .out(shifter_5_out));
  Shifter #(.width(32), .shift("lr")) shifter_6 (.in(and_3_out), .\dist (5'b10101), .out(shifter_6_out));
  Shifter #(.width(32), .shift("lr")) shifter_7 (.in(and_4_out), .\dist (5'b10000), .out(shifter_7_out));
  Shifter #(.width(32), .shift("lr")) shifter_8 (.in(and_5_out), .\dist (5'b01011), .out(shifter_8_out));
  Shifter #(.width(32), .shift("lr")) shifter_9 (.in(and_6_out), .\dist (5'b00110), .out(shifter_9_out));
  Shifter #(.width(32), .shift("lr")) shifter_10 (.in(and_7_out), .\dist ({5{1'b0}}), .out(shifter_10_out));
  Shifter #(.width(32), .shift("lr")) shifter_11 (.in(and_8_out), .\dist ({5{1'b0}}), .out(shifter_11_out));
  Shifter #(.width(32), .shift("lr")) shifter_12 (.in(and_9_out), .\dist ({5{1'b0}}), .out(shifter_12_out));
  Comparator #(.width(6)) comparator_22 (.a(funct), .b(6'b100000), .eq(comparator_22_eq));  // open: gt, lt
  Comparator #(.width(6)) comparator_23 (.a(funct), .b(6'b100001), .eq(comparator_23_eq));  // open: gt, lt
  Comparator #(.width(6)) comparator_24 (.a(funct), .b(6'b100010), .eq(comparator_24_eq));  // open: gt, lt
  Comparator #(.width(6)) comparator_25 (.a(funct), .b(6'b100011), .eq(comparator_25_eq));  // open: gt, lt
  Comparator #(.width(6)) comparator_26 (.a(funct), .b(6'b100100), .eq(comparator_26_eq));  // open: gt, lt
  Comparator #(.width(6)) comparator_27 (.a(funct), .b(6'b100101), .eq(comparator_27_eq));  // open: gt, lt
  Comparator #(.width(6)) comparator_28 (.a(funct), .b(6'b101010), .eq(comparator_28_eq));  // open: gt, lt
  Comparator #(.width(6)) comparator_29 (.a(funct), .b(6'b101011), .eq(comparator_29_eq));  // open: gt, lt
  Comparator #(.width(6)) comparator_30 (.a(funct), .b(6'b001000), .eq(comparator_30_eq));  // open: gt, lt
  Comparator #(.width(6)) comparator_31 (.a(funct), .b({6{1'b0}}), .eq(comparator_31_eq));  // open: gt, lt
  Comparator #(.width(6)) comparator_32 (.a(funct), .b(6'b000010), .eq(comparator_32_eq));  // open: gt, lt
  Comparator #(.width(6)) comparator_33 (.a(funct), .b(6'b000011), .eq(comparator_33_eq));  // open: gt, lt
  Comparator #(.width(6)) comparator_34 (.a(funct), .b(6'b111110), .eq(comparator_34_eq));  // open: gt, lt
  Comparator #(.width(6)) comparator_35 (.a(funct), .b({6{1'b1}}), .eq(comparator_35_eq));  // open: gt, lt
  not not_4 (not_4_out, ALU_equal);
  LED led_1 (.in(ALU_signed_overflow));
  alu_main ALU (
    .Switch__S(switch), .X(Data1), .Equal(ALU_equal), .RESULT(ALU_result_2),
    .Signed_Overflow(ALU_signed_overflow), .Y(multiplexer_22_out));
  or or_10 (_2addu, addu, addiu);
  or or_11 (_2and, \and , andi);
  or or_12 (_2or, \or , ori);
  or or_13 (_4add, add, lb, lw, Memwrite_t);
  or or_14 (_3addu, _2addu, lbu);
  Multiplexer #(.width(32)) multiplexer_24 (
    .in0(dataout), .in1(multiplexer_23_out), .out(Mem_out), .sel(\byte ));  // open: en
  Comparator #(.width(5), .mode("unsigned")) comparator_36 (
    .a(write_dst), .b(5'b01000), .eq(comparator_36_eq));  // open: gt, lt
  Comparator #(.width(5), .mode("unsigned")) comparator_37 (
    .a(write_dst), .b(5'b01001), .eq(comparator_37_eq));  // open: gt, lt
  Comparator #(.width(5), .mode("unsigned")) comparator_38 (
    .a(write_dst), .b(5'b01010), .eq(comparator_38_eq));  // open: gt, lt
  Comparator #(.width(5), .mode("unsigned")) comparator_39 (
    .a(write_dst), .b(5'b01011), .eq(comparator_39_eq));  // open: gt, lt
  or or_15 (or_15_out, j, jr, beq, bne, Memwrite_t);
  Bit_Extender #(.in_width(32), .out_width(6)) bit_extender_9 (.in(shifter_5_out), .out(op_t));
  Bit_Extender #(.in_width(32), .out_width(5)) bit_extender_10 (.in(shifter_6_out), .out(RS));
  Bit_Extender #(.in_width(32), .out_width(5)) bit_extender_11 (.in(shifter_7_out), .out(RT));
  Bit_Extender #(.in_width(32), .out_width(5)) bit_extender_12 (.in(shifter_8_out), .out(rd));
  Bit_Extender #(.in_width(32), .out_width(5)) bit_extender_13 (.in(shifter_9_out), .out(shamt));
  Bit_Extender #(.in_width(32), .out_width(6)) bit_extender_14 (.in(shifter_10_out), .out(funct));
  Bit_Extender #(.in_width(32)) bit_extender_15 (.in(shifter_11_out), .out(immediate));
  Bit_Extender #(.in_width(32), .out_width(26)) bit_extender_16 (.in(shifter_12_out), .out(addresss));
  and and_10 (add, comparator_22_eq, Rtype);
  and and_11 (addu, comparator_23_eq, Rtype);
  and and_12 (sub, comparator_24_eq, Rtype);
  and and_13 (subu, comparator_25_eq, Rtype);
  and and_14 (\and , comparator_26_eq, Rtype);
  and and_15 (\or , comparator_27_eq, Rtype);
  and and_16 (slt, comparator_28_eq, Rtype);
  and and_17 (sltu, comparator_29_eq, Rtype);
  and and_18 (jr, comparator_30_eq, Rtype);
  and and_19 (sll, comparator_31_eq, Rtype);
  and and_20 (srl, comparator_32_eq, Rtype);
  and and_21 (sra, comparator_33_eq, Rtype);
  and and_22 (bitpal, comparator_34_eq, Rtype);
  and and_23 (lfsr, comparator_35_eq, Rtype);
  Multiplexer #(.width(32)) multiplexer_25 (
    .in0(rsout0), .in1(RS_READ_VALUE), .out(Data1), .sel(rs_not_t));  // open: en
  Multiplexer #(.width(32)) multiplexer_26 (
    .in0(rtout0), .in1(RT_READ_VALUE), .out(multiplexer_26_out), .sel(rt_not_t));  // open: en
  assign bit_extender_17_out = {{27{1'b0}}, shamt};  // Bit_Extender bit_extender_17
  Multiplexer multiplexer_27 (.in0(op), .in1(op_2), .out(MemWrite), .sel(op_3), .en(undriven));
  and and_24 (beq_true, beq, ALU_equal);
  or or_16 (or_16_out, comparator_36_eq, comparator_37_eq, comparator_38_eq, comparator_39_eq);
  not not_5 (not_5_out, or_15_out);
  Demultiplexer #(.enable("false")) demultiplexer_1 (
    .out0(t_write_enable), .out1(RD_WRITE_ENABLE), .in(not_5_out), .sel(write_dst_not_t));
  or or_17 (branch_true, beq_true, bne_true);
  or or_18 (jump, j, jal);
  Multiplexer #(.width(2)) multiplexer_28 (
    .in0(2'b00), .in1(2'b01), .out(branch_value), .sel(branch_true));  // open: en
  Multiplexer #(.width(2)) multiplexer_29 (.in0(2'b00), .in1(2'b10), .out(jump_value), .sel(jump));  // open: en
  Multiplexer #(.width(2)) multiplexer_30 (.in0(2'b00), .in1(2'b11), .out(jr_value), .sel(jr));  // open: en
  // Probe on op_t
  // Probe on RS
  // Probe on RT
  // Probe on rd
  // Probe on shamt
  Multiplexer #(.width(32)) multiplexer_31 (
    .in0(multiplexer_26_out), .in1(bit_extender_17_out), .out(Data2), .sel(shift));  // open: en
  not not_6 (write_dst_not_t, or_16_out);
  assign choose = branch_value | jump_value | jr_value;  // OR_Gate or_19, 2 bits wide
  // Probe on funct
  // Probe on immediate
  // Probe on addresss
  Multiplexer #(.width(32)) multiplexer_32 (
    .in0(ALU_result_2), .in1(lui_imme), .out(alu_result), .sel(lui));  // open: en

  // Other names for the same wires on the sheet: FETCH_ADDRES[23:0] = FETCH_ADDRESS; pccount[23:0] = FETCH_ADDRESS;
  //   RT_READ_VALU[31:0] = RT_READ_VALUE; sw = Memwrite_t; RD_WRITE_VALU[31:0] = RD_WRITE_VALUE;
  //   write_data[31:0] = RD_WRITE_VALUE

  // Notes on the sheet:
  //   These are outputs/inputs from run.circ
  //   alu switch
  //   Select function
  //   Data Preparation
  //   Mem
  //   Write back
  //   Instruction Fetch
  //   alu
  //   Decode
  //   TEST
endmodule
