// Logisim project mem.circ as structural Verilog: 1 circuit, main circuit main
module main (
  input  [31:0] Data_Mem_Addr,
  input  [31:0] Data_Mem_In,
  input  CLOCK,
  input  ACCESS_BYTE,
  input  MEM_WRITE,
  output [31:0] Data_Mem_Out
);

  wire not_1_out;
  wire [31:0] subtractor_1_out;

  Subtractor #(.width(32)) subtractor_1 (
    .a(Data_Mem_Addr), .b(32'h10010000), .out(subtractor_1_out));  // open: bin, bout
  not not_1 (not_1_out, MEM_WRITE);
  assign Data_Mem_Out = MEM_WRITE ? Data_Mem_In : 32'bz;  // Controlled_Buffer controlled_buffer_1
  RAM #(.addrWidth(24), .dataWidth(32)) ram_1 (
    .addr(subtractor_1_out[31:8]), .data(Data_Mem_Out), .sel(1'b1), .clk(CLOCK), .ld(not_1_out), .clr(1'b0));

  // Notes on the sheet:
  //   These are INPUTS to the circuit
  //   DO NOT CHANGE THE LOCATIONS OF THE INPUTS/OUTPUTS! IF YOU DO SO, YOU NEED TO MAKE SURE THE PINS ARE AT THE RIGHT PLACE!
  //   This is an OUTPUT to the circuit
endmodule
