// Logisim project alu.circ as structural Verilog: 2 circuits, main circuit main
module main (
  input  [31:0] X,
  input  [5:0] Switch__S,
  input  [31:0] Y,
  output Equal,
  output Signed_Overflow,
  output [31:0] RESULT
);

  wire add_funct, add_overflow, comparator_1_gt, comparator_2_gt, comparator_3_eq, comparator_6_eq,
       comparator_7_lt, comparator_8_lt, comparator_9_eq, multiplexer_3_out, multiplexer_4_out, not_1_out,
       not_2_out, not_3_out, same_top_bit, sub_funct, sub_overflow, xor_1_out, xor_2_out;
  wire [1:0] adder_2_out, bit_extender_2_out, bit_extender_3_out;
  wire [4:0] bit_extender_1_out, bit_extender_4_out, bit_extender_5_out, bit_extender_6_out;
  wire [5:0] multiplexer_2_out, subtractor_1_out, subtractor_3_out;
  wire [15:0] converse_1_out;
  wire [31:0] add, addu, \and , bitpal, lfsr, \or , shifter_4_out, sll, slt, sltu, sra, srl, sub, subu;

  Comparator #(.width(6), .mode("unsigned")) comparator_1 (
    .a(Switch__S), .b(6'b111101), .gt(comparator_1_gt));  // open: eq, lt
  Comparator #(.width(6), .mode("unsigned")) comparator_2 (
    .a(Switch__S), .b(6'b011111), .gt(comparator_2_gt));  // open: eq, lt
  // Probe on Switch__S
  Bit_Extender #(.in_width(32), .out_width(5)) bit_extender_1 (.in(Y), .out(bit_extender_1_out));
  Subtractor #(.width(6)) subtractor_1 (.a(Switch__S), .b(6'b100000), .out(subtractor_1_out));  // open: bin, bout
  assign bit_extender_2_out = {{1{1'b0}}, comparator_1_gt};  // Bit_Extender bit_extender_2
  assign bit_extender_3_out = {{1{1'b0}}, comparator_2_gt};  // Bit_Extender bit_extender_3
  Subtractor #(.width(32)) subtractor_2 (.a(X), .b(Y), .out(subu));  // open: bin, bout
  assign \and  = X & Y;  // AND_Gate and_1, 32 bits wide
  Shifter #(.width(32)) shifter_1 (.in(X), .\dist (bit_extender_1_out), .out(sll));
  Adder #(.width(32)) adder_1 (.a(X), .b(Y), .out(add));  // open: cin, cout
  not not_1 (not_1_out, comparator_3_eq);
  Comparator #(.width(1)) comparator_3 (.a(X[31]), .b(add[31]), .eq(comparator_3_eq));  // open: gt, lt
  Adder #(.width(2)) adder_2 (.a(bit_extender_2_out), .b(bit_extender_3_out), .out(adder_2_out));  // open: cin, cout
  Subtractor #(.width(6)) subtractor_3 (.a(Switch__S), .b(6'b011100), .out(subtractor_3_out));  // open: bin, bout
  // Probe on Y
  Multiplexer #(.enable("false")) multiplexer_1 (.in0(1'b0), .in1(not_1_out), .out(add_overflow), .sel(same_top_bit));
  Multiplexer #(.select(2), .width(6)) multiplexer_2 (
    .in0(Switch__S), .in1(subtractor_3_out), .in2(subtractor_1_out), .out(multiplexer_2_out),
    .sel(adder_2_out));  // open: in3, en
  // Probe on X
  Bit_Extender #(.in_width(6), .out_width(5)) bit_extender_4 (.in(multiplexer_2_out), .out(bit_extender_4_out));
  // Probe on multiplexer_2_out
  Adder #(.width(32)) adder_3 (.a(X), .b(Y), .out(addu));  // open: cin, cout
  assign \or  = X | Y;  // OR_Gate or_1, 32 bits wide
  Bit_Extender #(.in_width(32), .out_width(5)) bit_extender_5 (.in(Y), .out(bit_extender_5_out));
  Comparator #(.width(32)) comparator_4 (.a(X), .b(Y), .eq(Equal));  // open: gt, lt
  Comparator #(.width(1)) comparator_5 (.a(X[31]), .b(Y[31]), .eq(same_top_bit));  // open: gt, lt
  Shifter #(.width(32), .shift("lr")) shifter_2 (.in(X), .\dist (bit_extender_5_out), .out(srl));
  Multiplexer #(.enable("false")) multiplexer_3 (
    .in0(add_overflow), .in1(1'b0), .out(multiplexer_3_out), .sel(add_funct));
  Multiplexer #(.enable("false")) multiplexer_4 (
    .in0(1'b0), .in1(sub_overflow), .out(multiplexer_4_out), .sel(sub_funct));
  Comparator #(.width(1)) comparator_6 (.a(X[31]), .b(sub[31]), .eq(comparator_6_eq));  // open: gt, lt
  Comparator #(.width(32)) comparator_7 (.a(X), .b(Y), .lt(comparator_7_lt));  // open: gt, eq
  Comparator #(.width(32)) comparator_8 (.a(X), .b(Y), .lt(comparator_8_lt));  // open: gt, eq
  Bit_Extender #(.in_width(32), .out_width(5)) bit_extender_6 (.in(Y), .out(bit_extender_6_out));
  Subtractor #(.width(32)) subtractor_4 (.a(X), .b(Y), .out(sub));  // open: bin, bout
  not not_2 (not_2_out, comparator_6_eq);
  or or_2 (Signed_Overflow, multiplexer_3_out, multiplexer_4_out);
  Multiplexer #(.select(5), .width(32), .enable("false")) multiplexer_5 (
    .in0(sll), .in2(srl), .in3(sra), .in4(add), .in5(addu), .in6(sub), .in7(subu), .in8(\and ), .in9(\or ),
    .in14(slt), .in16(sltu), .in30(bitpal), .in31(lfsr), .out(RESULT), .sel(bit_extender_4_out));  // open: in1, in10, in11, in12, in13, in15, in17, in18, in19, in20, in21, in22, in23, in24, in25, in26, in27, in28, in29
  not not_3 (not_3_out, same_top_bit);
  Multiplexer #(.enable("false")) multiplexer_6 (.in0(1'b0), .in1(not_2_out), .out(sub_overflow), .sel(not_3_out));
  assign sltu = {{31{1'b0}}, comparator_7_lt};  // Bit_Extender bit_extender_7
  assign slt = {{31{1'b0}}, comparator_8_lt};  // Bit_Extender bit_extender_8
  Shifter #(.width(32), .shift("ar")) shifter_3 (.in(X), .\dist (bit_extender_6_out), .out(sra));
  converse converse_1 (.in_1(X[15:0]), .out(converse_1_out));
  xor xor_1 (xor_1_out, X[0], X[2]);
  xor xor_2 (xor_2_out, xor_1_out, X[3]);
  Comparator #(.width(16)) comparator_9 (.a(converse_1_out), .b(X[31:16]), .eq(comparator_9_eq));  // open: gt, lt
  xor xor_3 (lfsr[31], xor_2_out, X[5]);
  Shifter #(.width(32), .shift("lr")) shifter_4 (.in(X), .\dist (5'b00001), .out(shifter_4_out));
  Comparator #(.width(6)) comparator_10 (.a(Switch__S), .b(6'b100000), .eq(add_funct));  // open: gt, lt
  Comparator #(.width(6)) comparator_11 (.a(Switch__S), .b(6'b100010), .eq(sub_funct));  // open: gt, lt
  assign bitpal = {{31{1'b0}}, comparator_9_eq};  // Bit_Extender bit_extender_9
  Bit_Extender #(.in_width(32), .out_width(31)) bit_extender_10 (.in(shifter_4_out), .out(lfsr[30:0]));

  // Other names for the same wires on the sheet: add_tbit = add[31]; iff_equal = Equal; sub_tbit = sub[31];
  //   switch[5:0] = Switch__S; x_input[31:0] = X; y_input[31:0] = Y

  // Notes on the sheet:
  //   INPUTS to your circuit
  //   SUBU (Subtraction Unsigned)
  //   AND (Boolean &)
  //   SLL (Shift Left Logical)
  //   # shamt -> 5 bits
  //   ADD (Addition)
  //   # Signed overflow if top bit is incorrectly found
  //   # If top two bits are not same, then will not overflow (sum -> 0)
  //   # If top two bits are same, different top bit for func -> overflow 
  //   # Subtract's 16 if 1 at 5th bit
  //   # (Needed to fit in mux)
  //   Core ALU (MIPS) Functions
  //   ADDU (Addition Unsigned)
  //   OR (Boolean |)
  //   SRL (Shift Right Logical)
  //   # shamt -> 5 bits
  //   IFF Equal Test
  //   # must extend to maintain size of commands
  //   Overflow Detection
  //   # Use splitter (from lab 6) to grab only most significant (top) bit
  //   DON'T CHANGE THE INPUTS AND OUTPUTS! IF YOU DO SO, YOU NEED TO MAKE SURE THE PINS ARE IN THE RIGHT PLACES!
  //   # Signed Overflow occurs only with add or sub 
  //   SUB (Subtraction)
  //   # Signed overflow if top bit is incorrectly found
  //   # If top two bits same, then will not overflow (diff -> 0)
  //   # If top two bits are not same, different top bit for func -> overflow 
  //   SLTU (Set Less Than Unsigned)
  //   SLT (Set Less Than)
  //   SRA (Shift Right Arithmatic)
  //   # shamt -> 5 bits
  //   OUTPUTS of your circuit
  //   Add Function is 16 in mex
  //   Sub Function is 18 in mux
endmodule

module converse (
  input  [15:0] in_1,
  output [15:0] out
);


  assign out = {in_1[0], in_1[1], in_1[2], in_1[3], in_1[4], in_1[5], in_1[6], in_1[7], in_1[8], in_1[9], in_1[10], in_1[11], in_1[12], in_1[13], in_1[14], in_1[15]};
endmodule
